# Fritzing sketch circuito1 (saved by Fritzing 0.9.3b)
breadboards: 1

parts:
  S1 = Pushbutton [package="[THT]"]
  Raspberry_Pi1 = Raspberry Pi B+
  R1 = Resistor [tolerance=±5% resistance=1k package="0603 [SMD]"]
  R2 = Resistor [tolerance=±5% resistance=10k package="0603 [SMD]"]
  R3 = Resistor [tolerance=±5% resistance=1k package="0603 [SMD]"]
  LED1 = LED - 5mm [color="White (8000K)" package="5 mm [THT]"]  # not connected
  Componente1 = InvenSense MPU6050

nets:
  N1: S1.Pin_1, S1.Pin_2, R3.Pin_0
  N2: S1.Pin_3, S1.Pin_4, Raspberry_Pi1.GPIO27, R2.Pin_0
  3V3: Raspberry_Pi1.3v3, R3.Pin_1, Componente1.VCC
  N3: Raspberry_Pi1.GPIO2, Componente1.SDA
  N4: Raspberry_Pi1.GPIO3, Componente1.SCL
  GND: Raspberry_Pi1.GND, R1.Pin_0, R2.Pin_1, Componente1.GND
